// Logisim project Ejercicio8.circ as structural Verilog: 5 circuits, main circuit main
module main (
  input  [5:0] in_1,
  input  [5:0] in_2,
  output [5:0] out_3
);

  wire inverter_1_out_7, inverter_1_out_8, inverter_1_out_9, inverter_1_out_10, inverter_1_out_11,
       inverter_1_out_12, sumador_completo_1_cout, sumador_completo_2_cout, sumador_completo_3_cout,
       sumador_completo_4_cout, sumador_completo_5_cout, sumador_completo_6_cout;

  sumador_completo sumador_completo_1 (
    .Cin(sumador_completo_2_cout), .A(in_2[5]), .B(inverter_1_out_7), .S(out_3[5]),
    .Cout(sumador_completo_1_cout));
  sumador_completo sumador_completo_2 (
    .Cin(sumador_completo_3_cout), .A(in_2[4]), .B(inverter_1_out_8), .S(out_3[4]),
    .Cout(sumador_completo_2_cout));
  sumador_completo sumador_completo_3 (
    .Cin(sumador_completo_4_cout), .A(in_2[3]), .B(inverter_1_out_9), .S(out_3[3]),
    .Cout(sumador_completo_3_cout));
  sumador_completo sumador_completo_4 (
    .Cin(sumador_completo_5_cout), .A(in_2[2]), .B(inverter_1_out_10), .S(out_3[2]),
    .Cout(sumador_completo_4_cout));
  sumador_completo sumador_completo_5 (
    .Cin(sumador_completo_6_cout), .A(in_2[1]), .B(inverter_1_out_11), .S(out_3[1]),
    .Cout(sumador_completo_5_cout));
  inverter inverter_1 (
    .in_1(in_1[5]), .in_2(in_1[4]), .in_3(in_1[3]), .in_4(in_1[2]), .in_5(in_1[1]), .in_6(in_1[0]),
    .out_7(inverter_1_out_7), .out_8(inverter_1_out_8), .out_9(inverter_1_out_9), .out_10(inverter_1_out_10),
    .out_11(inverter_1_out_11), .out_12(inverter_1_out_12));
  sumador_completo sumador_completo_6 (
    .Cin(1'b0), .A(in_2[0]), .B(inverter_1_out_12), .S(out_3[0]), .Cout(sumador_completo_6_cout));
endmodule

module sumador_completo (
  input  Cin,
  input  A,
  input  B,
  output S,
  output Cout
);

  wire and_1_out, and_2_out, xor_1_out;

  xor xor_1 (xor_1_out, Cin, A);
  and and_1 (and_1_out, A, Cin);
  xor xor_2 (S, xor_1_out, B);
  and and_2 (and_2_out, B, xor_1_out);
  or or_1 (Cout, and_2_out, and_1_out);
endmodule

module inverter (
  input  in_1,
  input  in_2,
  input  in_3,
  input  in_4,
  input  in_5,
  input  in_6,
  output out_7,
  output out_8,
  output out_9,
  output out_10,
  output out_11,
  output out_12
);

  not not_1 (out_7, in_1);
  not not_2 (out_9, in_3);
  not not_3 (out_8, in_2);
  not not_4 (out_12, in_6);
  not not_5 (out_11, in_5);
  not not_6 (out_10, in_4);
endmodule

module inverso_aditivo_enable (
  input  [5:0] in_1,
  input  [5:0] in_2,
  input  EN,
  output [5:0] out_4
);

  wire inverter_1_out_7, inverter_1_out_8, inverter_1_out_9, inverter_1_out_10, inverter_1_out_11,
       inverter_1_out_12, sumador_completo_1_cout, sumador_completo_1_s, sumador_completo_2_cout,
       sumador_completo_2_s, sumador_completo_3_cout, sumador_completo_3_s, sumador_completo_4_cout,
       sumador_completo_4_s, sumador_completo_5_cout, sumador_completo_5_s, sumador_completo_6_cout,
       sumador_completo_6_s;

  and and_1 (out_4[5], EN, sumador_completo_1_s);
  sumador_completo sumador_completo_1 (
    .Cin(sumador_completo_2_cout), .A(in_2[5]), .B(inverter_1_out_7), .S(sumador_completo_1_s),
    .Cout(sumador_completo_1_cout));
  and and_2 (out_4[4], EN, sumador_completo_2_s);
  sumador_completo sumador_completo_2 (
    .Cin(sumador_completo_3_cout), .A(in_2[4]), .B(inverter_1_out_8), .S(sumador_completo_2_s),
    .Cout(sumador_completo_2_cout));
  sumador_completo sumador_completo_3 (
    .Cin(sumador_completo_4_cout), .A(in_2[3]), .B(inverter_1_out_9), .S(sumador_completo_3_s),
    .Cout(sumador_completo_3_cout));
  and and_3 (out_4[3], EN, sumador_completo_3_s);
  sumador_completo sumador_completo_4 (
    .Cin(sumador_completo_5_cout), .A(in_2[2]), .B(inverter_1_out_10), .S(sumador_completo_4_s),
    .Cout(sumador_completo_4_cout));
  and and_4 (out_4[2], EN, sumador_completo_4_s);
  and and_5 (out_4[1], EN, sumador_completo_5_s);
  sumador_completo sumador_completo_5 (
    .Cin(sumador_completo_6_cout), .A(in_2[1]), .B(inverter_1_out_11), .S(sumador_completo_5_s),
    .Cout(sumador_completo_5_cout));
  and and_6 (out_4[0], EN, sumador_completo_6_s);
  inverter inverter_1 (
    .in_1(in_1[5]), .in_2(in_1[4]), .in_3(in_1[3]), .in_4(in_1[2]), .in_5(in_1[1]), .in_6(in_1[0]),
    .out_7(inverter_1_out_7), .out_8(inverter_1_out_8), .out_9(inverter_1_out_9), .out_10(inverter_1_out_10),
    .out_11(inverter_1_out_11), .out_12(inverter_1_out_12));
  sumador_completo sumador_completo_6 (
    .Cin(1'b0), .A(in_2[0]), .B(inverter_1_out_12), .S(sumador_completo_6_s), .Cout(sumador_completo_6_cout));
endmodule

module ejercicio9 (
  input  [3:0] in_1,
  input  [3:0] in_2,
  input  in_3,
  input  in_4,
  output [3:0] out_5
);

  wire multiplexer_1_out, multiplexer_2_out, multiplexer_3_out, multiplexer_4_out, not_1_out, not_2_out,
       not_3_out, not_4_out, sumador_completo_1_cout, sumador_completo_2_cout, sumador_completo_3_cout,
       sumador_completo_4_cout;

  not not_1 (not_1_out, in_1[3]);
  Multiplexer multiplexer_1 (.in0(in_1[3]), .in1(not_1_out), .out(multiplexer_1_out), .sel(in_3), .en(in_4));
  sumador_completo sumador_completo_1 (
    .Cin(sumador_completo_2_cout), .A(multiplexer_1_out), .B(in_2[3]), .S(out_5[3]),
    .Cout(sumador_completo_1_cout));
  not not_2 (not_2_out, in_1[2]);
  Multiplexer multiplexer_2 (.in0(in_1[2]), .in1(not_2_out), .out(multiplexer_2_out), .sel(in_3), .en(in_4));
  sumador_completo sumador_completo_2 (
    .Cin(sumador_completo_3_cout), .A(multiplexer_2_out), .B(in_2[2]), .S(out_5[2]),
    .Cout(sumador_completo_2_cout));
  not not_3 (not_3_out, in_1[1]);
  Multiplexer multiplexer_3 (.in0(in_1[1]), .in1(not_3_out), .out(multiplexer_3_out), .sel(in_3), .en(in_4));
  sumador_completo sumador_completo_3 (
    .Cin(sumador_completo_4_cout), .A(multiplexer_3_out), .B(in_2[1]), .S(out_5[1]),
    .Cout(sumador_completo_3_cout));
  not not_4 (not_4_out, in_1[0]);
  Multiplexer multiplexer_4 (.in0(in_1[0]), .in1(not_4_out), .out(multiplexer_4_out), .sel(in_3), .en(in_4));
  sumador_completo sumador_completo_4 (
    .Cin(1'b0), .A(multiplexer_4_out), .B(in_2[0]), .S(out_5[0]), .Cout(sumador_completo_4_cout));
endmodule
